// Logisim project CPU.circ as structural Verilog: 4 circuits, main circuit main
module main (
  input  in_1,
  input  in_2,
  input  in_3,
  input  in_4,
  input  [17:0] _18_Bit_Input
);

  _2x4Decoder _2x4_Decoder (.A(_18_Bit_Input[0]), .B(_18_Bit_Input[1]), .D0(in_1), .D1(in_2), .D2(in_3), .D3(in_4));
  Timer timer_1 ();  // open: Increment, Clock, Clear, T0, T1, T2, T3, T4, T5, T6, T7, T8, T9, T10, T11, T12, T13, T14, T15, Overflow
endmodule

module Timer (
  input  Increment,
  input  Clock,
  input  Clear,
  output T0,
  output T1,
  output T2,
  output T3,
  output T4,
  output T5,
  output T6,
  output T7,
  output T8,
  output T9,
  output T10,
  output T11,
  output T12,
  output T13,
  output T14,
  output T15,
  output Overflow
);

  wire [3:0] counter_1_q;

  Counter #(.width(4), .max('hf)) counter_1 (
    .count(Increment), .Q(counter_1_q), .carry(Overflow), .clk(Clock), .clr(Clear));  // open: load, D
  Decoder #(.select(4)) decoder_1 (
    .out0(T0), .out1(T1), .out2(T2), .out3(T3), .out4(T4), .out5(T5), .out6(T6), .out7(T7), .out8(T8),
    .out9(T9), .out10(T10), .out11(T11), .out12(T12), .out13(T13), .out14(T14), .out15(T15), .sel(counter_1_q));  // open: en
endmodule

module Bus (
  input  [11:0] in_1,
  input  [11:0] in_2,
  input  [11:0] in_3,
  input  [11:0] in_4,
  input  [11:0] in_5,
  input  [11:0] in_6,
  input  [17:0] in_7,
  input  [7:0] in_8,
  input  [7:0] in_9
);

  wire undriven, undriven_2, undriven_3, undriven_4, undriven_5, undriven_6, undriven_7, undriven_8,
       undriven_9;

  Multiplexer #(.select(4)) multiplexer_1 (
    .in0(undriven), .in1(undriven_2), .in2(undriven_3), .in3(undriven_4), .in4(undriven_5), .in5(undriven_8),
    .in6(undriven_6), .in7(undriven_7), .in8(undriven_9));  // open: in9, in10, in11, in12, in13, in14, in15, out, sel, en
endmodule

module _2x4Decoder (
  input  A,
  input  B,
  output D0,
  output D1,
  output D2,
  output D3
);

  wire not_1_out, not_2_out;

  nor nor_1 (D0, A, B);
  not not_1 (not_1_out, A);
  not not_2 (not_2_out, B);
  and and_1 (D1, not_1_out, B);
  and and_2 (D2, A, not_2_out);
  and and_3 (D3, A, B);
endmodule
